// Logisim project cpu.circ as structural Verilog
module ALU (
  input  [3:0] Flags,
  input  [15:0] a,
  input  [15:0] b,
  input  [15:0] c,
  input  [4:0] CMD,
  output [3:0] flagsOut,
  output [15:0] R
);

  wire adder_1_cout, adder_2_cout, adder_3_cout, adder_4_cout, subtractor_1_bout;
  wire [15:0] adder_1_out, adder_2_out, adder_3_out, adder_4_out, subtractor_1_out;

  Adder #(.width(16)) adder_1 (.a(a), .b(b), .out(adder_1_out), .cin(Flags[0]), .cout(adder_1_cout));
  Adder #(.width(16)) adder_2 (.a(a), .b(b), .out(adder_2_out), .cout(adder_2_cout));  // open: cin
  Adder #(.width(16)) adder_3 (.a(adder_1_out), .b(c), .out(adder_3_out), .cin(adder_1_cout), .cout(adder_3_cout));
  Adder #(.width(16)) adder_4 (.a(a), .b(b), .out(adder_4_out), .cin(Flags[0]), .cout(adder_4_cout));
  Subtractor #(.width(16)) subtractor_1 (
    .a(a), .b(b), .out(subtractor_1_out), .bin(Flags[0]), .bout(subtractor_1_bout));
  nor16 nor16_1 (.in_1(R), .out_2(flagsOut[2]));
  Multiplexer #(.select(5)) multiplexer_1 (
    .in0(adder_2_cout), .in1(adder_3_cout), .in2(adder_4_cout), .in3(subtractor_1_bout), .out(flagsOut[0]),
    .sel(CMD));  // open: in4, in5, in6, in7, in8, in9, in10, in11, in12, in13, in14, in15, in16, in17, in18, in19, in20, in21, in22, in23, in24, in25, in26, in27, in28, in29, in30, in31
  Multiplexer #(.select(5), .width(16)) multiplexer_2 (
    .in0(adder_2_out), .in1(adder_3_out), .in2(adder_4_out), .in3(subtractor_1_out), .out(R), .sel(CMD));  // open: in4, in5, in6, in7, in8, in9, in10, in11, in12, in13, in14, in15, in16, in17, in18, in19, in20, in21, in22, in23, in24, in25, in26, in27, in28, in29, in30, in31

  // Notes on the sheet:
  //   ADD a b c
  //   ADD a b
  //   ADD a b carry
  //   SUB a b
  //   Zero Flag 2
  //   Carry Flag 0
endmodule

module CU (
  input  CLK,
  input  [19:0] PMemBus,
  input  Reset,
  output out_4,
  output out_5,
  output out_6,
  output out_7
);

  wire Stages_carry;
  wire [1:0] Stages_q;

  Register #(.width(20)) register_1 (.D(PMemBus), .en(1'b1), .clk(CLK), .clr(Reset));  // open: Q
  Counter #(.max('h3), .width(2)) Stages (
    .clk(CLK), .carry(Stages_carry), .Q(Stages_q));  // open: clr, load, up, count, D
  ROM #(.addrWidth(10)) MikroOp (.addr({PMemBus[7:0], Stages_q}));  // open: data
  Demultiplexer #(.select(2)) demultiplexer_1 (
    .out0(out_4), .out1(out_5), .out2(out_6), .out3(out_7), .in(1'b1), .sel(Stages_q));
  Counter #(.max('hffff), .width(16)) ProgrammCounter (.clk(Stages_carry));  // open: clr, load, up, count, D, carry, Q
endmodule

module nor16 (
  input  [15:0] in_1,
  output out_2
);

  nor nor_1 (out_2, in_1[0], in_1[1], in_1[2], in_1[3], in_1[4], in_1[5], in_1[6], in_1[7], in_1[8], in_1[9], in_1[10], in_1[11], in_1[12], in_1[13], in_1[14], in_1[15]);
endmodule

module CPU_Register (
  input  CLK,
  input  Reset,
  input  [2:0] AddrINP,
  input  WE,
  input  [15:0] PortINP,
  input  [2:0] AddrC,
  input  [2:0] AddrB,
  input  [2:0] AddrA,
  output [15:0] PortA,
  output [15:0] PortB,
  output [15:0] PortC
);

  wire decoder_1_out0, decoder_1_out1, decoder_1_out2, decoder_1_out3, decoder_1_out4, decoder_1_out5,
       decoder_1_out6, decoder_1_out7;
  wire [15:0] register_1_q, register_2_q, register_3_q, register_4_q, register_5_q, register_6_q,
       register_7_q, register_8_q;

  Decoder #(.select(3)) decoder_1 (
    .out0(decoder_1_out0), .out1(decoder_1_out1), .out2(decoder_1_out2), .out3(decoder_1_out3),
    .out4(decoder_1_out4), .out5(decoder_1_out5), .out6(decoder_1_out6), .out7(decoder_1_out7),
    .sel(AddrINP), .en(WE));
  Register #(.width(16)) register_1 (.D(PortINP), .en(decoder_1_out0), .clk(CLK), .Q(register_1_q), .clr(Reset));
  Register #(.width(16)) register_2 (.D(PortINP), .en(decoder_1_out1), .clk(CLK), .Q(register_2_q), .clr(Reset));
  Register #(.width(16)) register_3 (.D(PortINP), .en(decoder_1_out2), .clk(CLK), .Q(register_3_q), .clr(Reset));
  Register #(.width(16)) register_4 (.D(PortINP), .en(decoder_1_out3), .clk(CLK), .Q(register_4_q), .clr(Reset));
  Register #(.width(16)) register_5 (.D(PortINP), .en(decoder_1_out4), .clk(CLK), .Q(register_5_q), .clr(Reset));
  Register #(.width(16)) register_6 (.D(PortINP), .en(decoder_1_out5), .clk(CLK), .Q(register_6_q), .clr(Reset));
  Register #(.width(16)) register_7 (.D(PortINP), .en(decoder_1_out6), .clk(CLK), .Q(register_7_q), .clr(Reset));
  Register #(.width(16)) register_8 (.D(PortINP), .en(decoder_1_out7), .clk(CLK), .Q(register_8_q), .clr(Reset));
  Demultiplexer #(.select(3), .width(16)) demultiplexer_1 (
    .out0(register_1_q), .out1(register_2_q), .out2(register_3_q), .out3(register_4_q), .out4(register_5_q),
    .out5(register_6_q), .out6(register_7_q), .out7(register_8_q), .in(PortC), .sel(AddrC));
  Demultiplexer #(.select(3), .width(16)) demultiplexer_2 (
    .out0(register_1_q), .out1(register_2_q), .out2(register_3_q), .out3(register_4_q), .out4(register_5_q),
    .out5(register_6_q), .out6(register_7_q), .out7(register_8_q), .in(PortA), .sel(AddrA));
  Demultiplexer #(.select(3), .width(16)) demultiplexer_3 (
    .out0(register_1_q), .out1(register_2_q), .out2(register_3_q), .out3(register_4_q), .out4(register_5_q),
    .out5(register_6_q), .out6(register_7_q), .out7(register_8_q), .in(PortB), .sel(AddrB));
endmodule
